# Fritzing sketch HSPin3v (saved by Fritzing 0.9.1b)
breadboards: 1

parts:
  Trinket = Trinket 3V
  DC_3_7V = DC Power [voltage=5]
  PN2222 = PNP-Transistor [package="TO92 [THT]"]
  MOTOR1 = Vibration Motor
  J1 = Infrared Proximity Sensor

nets:
  N1: Trinket.no_name_yet#1, DC_3_7V.V+, MOTOR1.POS, J1.Vcc
  N2: Trinket.no_name_yet#2, DC_3_7V.V-, PN2222.C, J1.GND
  N3: Trinket.no_name_yet#7, J1.Vout
  N4: Trinket.no_name_yet#9, PN2222.B
  N5: PN2222.E, MOTOR1.NEG

custom parts:
  Trinket 3V: Adafruit Trinket 3V
  Vibration Motor: An eccentric vibration motor!
